# Fritzing sketch esp32_propane_scale_v2 (saved by Fritzing 1.0.6)

parts:
  LR = Load Sensor - 50kg [part_number=SEN-10245]
  UL = Load Sensor - 50kg [part_number=SEN-10245]
  UR = Load Sensor - 50kg [part_number=SEN-10245]
  LL = Load Sensor - 50kg [part_number=SEN-10245]
  M1 = ESP-Prog [package=THT]
  LR_2 = screw terminal, 3 pins
  LL_2 = screw terminal, 3 pins
  UR_2 = screw terminal, 3 pins
  E+_E-_A-_A+ = screw terminal, 4 pins
  UL_2 = screw terminal, 3 pins
  proto1 = Adafruit_Permaproto_Full_sized_Board
  SparkFun_Load_Cell_Amplifier_-_HX2 = SparkFun Load Cell Amplifier - HX711 [part_number=SEN-13879]
  SparkFun_ESP32_Thing2 = SparkFun ESP32 Thing [part_number=DEV-13907]

nets:
  N1: LR.B, LR_2.pin1
  N2: LR.W, LR_2.pin2
  N3: LR.R, LR_2.pin3
  N4: UL.B, UL_2.pin3
  N5: UL.W, UL_2.pin2
  N6: UL.R, UL_2.pin1
  N7: UR.B, UR_2.pin3
  N8: UR.W, UR_2.pin2
  N9: UR.R, UR_2.pin1
  N10: LL.B, LL_2.pin1
  N11: LL.W, LL_2.pin2
  N12: LL.R, LL_2.pin3
  N13: M1.3V3-jtag, M1.VJTAG, M1.Vprog, M1.3V3-prog
  N14: M1.IO0_I, M1.IO0_O
  N15: M1.JTAG-ESP_TMS-.1, SparkFun_ESP32_Thing2.14
  N16: M1.JTAG-GND-3-.1, M1.JTAG-GND-5-.1, M1.JTAG-GND-7-.1, M1.JTAG-GND-9-.1, M1.Prog-GND-4-.1, proto1.connectorX54, proto1.connectorX57, proto1.connectorX58, proto1.connectorX59, proto1.connectorZ59
  N17: M1.JTAG-ESP-TCK-.1, SparkFun_ESP32_Thing2.13
  N18: M1.JAG-ESP-TDO-.1, SparkFun_ESP32_Thing2.15
  N19: M1.JTAG-ESP_TDI-.1, SparkFun_ESP32_Thing2.12
  N20: M1.Prog-ESP_EN-.1, proto1.connectorB55
  N21: M1.Prog-ESP_TXD-.1, SparkFun_ESP32_Thing2.U0RXD
  N22: M1.Prog-ESP_RXD-.1, SparkFun_ESP32_Thing2.U0TXD
  N23: M1.Prog-ESP_IO0-.1, proto1.connectorI52
  N24: E+_E-_A-_A+.pin1, SparkFun_Load_Cell_Amplifier_-_HX2.A+
  N25: E+_E-_A-_A+.pin2, SparkFun_Load_Cell_Amplifier_-_HX2.A-
  N26: E+_E-_A-_A+.pin3, proto1.connectorX29, SparkFun_Load_Cell_Amplifier_-_HX2.GND
  N27: E+_E-_A-_A+.pin4, SparkFun_Load_Cell_Amplifier_-_HX2.AVDD
  N28: proto1.connectorC1, proto1.connectorH1
  N29: proto1.connectorC2, proto1.connectorC17
  N30: proto1.connectorC16, proto1.connectorH16
  N31: proto1.connectorE3, proto1.connectorF25
  N32: proto1.connectorE18, proto1.connectorF22
  N33: proto1.connectorF3, proto1.connectorF23
  N34: proto1.connectorF18, proto1.connectorF24
  N35: proto1.connectorH2, proto1.connectorH17
  N36: proto1.connectorW33, SparkFun_Load_Cell_Amplifier_-_HX2.VDD
  N37: proto1.connectorW56, SparkFun_ESP32_Thing2.3.3V
  N38: proto1.connectorX60, proto1.connectorZ60, SparkFun_ESP32_Thing2.GND
  N39: proto1.connectorY35, SparkFun_Load_Cell_Amplifier_-_HX2.VCC
  N40: proto1.connectorY59, SparkFun_ESP32_Thing2.VUSB-RAW
  N41: SparkFun_Load_Cell_Amplifier_-_HX2.DAT, SparkFun_ESP32_Thing2.16
  N42: SparkFun_Load_Cell_Amplifier_-_HX2.SCK, SparkFun_ESP32_Thing2.17

notes:
  +/White
  -/Black
  C/Red
  E+
  A+
  A-
  E-
  3v3
  5V
  GND
  VBAT
  TDO
  TMS
  TDI
  TCK
  MOSI
  MISO
  SCK
  VDD
  RST
  RXD
  IO
  TXD
  NC

custom parts:
  Load Sensor - 50kg: Half-wheatstone bridge Load Cell modified from the Fritzing Repo This load sensor, sometimes called a strain gauge, is the same one found in digital bathroom scales (you know, the ones you use in January for your New Year's resolutions, and then forget about a month later). This sensor can measure up to about 110 pounds.
  ESP-Prog: Espressif ESP-Prog board. ESP-Prog is one of Espressif’s development and debugging tools, with functions including automatic firmware downloading, serial communication, and JTAG online debugging. ESP-Prog's automatic firmware downloading and serial communication functions are supported on both the ESP8266 and ESP32 platforms, while the JTAG online debugging is supported only on the ESP32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
  SparkFun Load Cell Amplifier - HX711: The SparkFun Load Cell Amplifier is a small breakout board for the HX711 IC that allows you to easily read load cells to measure weight. By connecting the amplifier to your microcontroller you will be able to read the changes in the resistance of the load cell, and with some calibration you’ll be able to get very accurate weight measurements. This can be handy for creating your own industrial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
  SparkFun ESP32 Thing: The SparkFun ESP32 Thing is a comprehensive development platform for Espressif’s ESP32, their super-charged version of the popular ESP8266. Like the 8266, the ESP32 is a WiFi-compatible microcontroller, but to that it adds support for Bluetooth low-energy (i.e BLE, BT4.0, Bluetooth Smart), and nearly 30 I/O pins. The ESP32’s power and versatility will make it the foundation of IoT and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
